# Fritzing sketch SCU-WSS_Arduino-sketch(2) (saved by Fritzing 0.9.2b)
breadboards: 1

parts:
  Part1 = Arduino Uno (Rev3)
  C1 = Electrolytic Capacitor [capacitance=10µF package="100 mil [THT, electrolytic]"]
  BLUEFRUIT1 = Adafruit Bluefruit EZ-LINK v1.0

nets:
  N1: Part1.D0/RX, BLUEFRUIT1.TX
  N2: Part1.D1/TX, BLUEFRUIT1.RX
  N3: Part1.RESET, C1.+
  5V: Part1.5V, BLUEFRUIT1.Vin
  GND: Part1.GND, BLUEFRUIT1.GND
  N4: C1.-, BLUEFRUIT1.DTR

custom parts:
  Adafruit Bluefruit EZ-LINK v1.0: Bluefruit EZ-LINK, Bluetooth Serial Link & Arduino Programmer
